# Fritzing sketch 37 in 1 - KY 015 (saved by Fritzing 0.9.3b)

parts:
  Componente1 = Arduino Uno (Rev3)
  J1 = male pin header, 3 pins [form="♂ (male)"]

nets:
  N1: Componente1.D13/SCK, J1.pin1
  N2: Componente1.D2, J1.pin2
  N3: Componente1.5V, J1.pin3

notes:
  KY 015 Temperature and humidity sensor module
