# Fritzing sketch main_SLAVE (saved by Fritzing 0.9.4)
breadboards: 1

parts:
  부품2 = Arduino Uno (Rev3)
  부품3 = Bluetooth HC-05 Macho
  Part1 = KY-019 5V Relay Module [package="Breakout board"]
  Part2 = KY-019 5V Relay Module [package="Breakout board"]
  Part3 = KY-019 5V Relay Module [package="Breakout board"]

nets:
  N1: 부품2.D8, Part1.S
  N2: 부품2.D9_PWM, Part2.S
  N3: 부품2.D10_PWM/SS, Part3.S
  N4: 부품2.D2, 부품3.TXD
  N5: 부품2.D3_PWM, 부품3.RXD
  5V: 부품2.5V, 부품3.VCC
  GND: 부품2.GND, 부품3.GND
  N6: Part1.+, Part2.+, Part3.+, Part3.-
  N7: Part1.-, Part2.-

notes:
  Relay_Light
  Relay_AirPurifier
  Relay_Humudifier

custom parts:
  KY-019 5V Relay Module: KY-019 5V Relay module, used to control AC circuits.
